// Logisim project cache.circ as structural Verilog: 9 circuits, main circuit MCU
module MCU (
  input  [31:0] PC,
  input  [31:0] Address,
  input  [31:0] Data_In,
  input  Write,
  input  Select,
  input  Clock,
  input  [2:0] Mode,
  output Wait_for_Instruction,
  output [31:0] Next_Instruction,
  output Wait_for_Data,
  output [31:0] Data_Out
);

  wire and_1_out, clock_1_out, comparator_1_eq, s_r_ff_1_qn;
  wire [31:0] adder_1_out, multiplexer_1_out, n32bit_increment_1_out, register_1_q, register_2_q;

  Clock clock_1 (.out(clock_1_out));
  Multiplexer #(.width(32), .disabled(0), .enable("false")) multiplexer_1 (
    .in0(n32bit_increment_1_out), .in1(PC), .out(multiplexer_1_out), .sel(s_r_ff_1_qn));
  L1_Cache l1_cache_1 (
    .Address(PC), .Mode(3'b100), .Clock(clock_1_out), .Write(1'b0), .Data_Out(Next_Instruction),
    .Cache_miss(Wait_for_Instruction), .Enable(1'b1));  // open: Data_in, Load_Address, Load_Data
  L1_Cache l1_cache_2 (
    .Address(Address), .Data_in(Data_In), .Mode(Mode), .Clock(clock_1_out), .Write(Write),
    .Data_Out(Data_Out), .Cache_miss(Wait_for_Data), .Enable(Select));  // open: Load_Address, Load_Data
  _32bit_increment u_32bit_increment_1 (.In(register_1_q), .Out(n32bit_increment_1_out));
  Register #(.width(32)) register_1 (.D(multiplexer_1_out), .Q(register_1_q), .clk(clock_1_out));  // open: en, clr
  Register #(.width(32)) register_2 (.D(PC), .en(s_r_ff_1_qn), .Q(register_2_q), .clk(clock_1_out));  // open: clr
  and and_1 (and_1_out, Wait_for_Instruction, ~comparator_1_eq);  // AND_Gate
  Adder #(.width(32)) adder_1 (.a(register_2_q), .b(32'h100), .out(adder_1_out));  // open: cin, cout
  S_R_Flip_Flop s_r_ff_1 (
    .S(and_1_out), .clk(clock_1_out), .R(comparator_1_eq), .Qn(s_r_ff_1_qn));  // open: Q, preset, reset, en
  Comparator #(.width(32)) comparator_1 (.a(register_1_q), .b(adder_1_out), .eq(comparator_1_eq));  // open: gt, lt

  // Notes on the sheet:
  //   I-Cache
  //   D-Cache
endmodule

module Cache_Line (
  input  Write,
  input  Set_Tag,
  input  Clock,
  input  [31:0] Address,
  input  Sel,
  input  [2:0] Mode,
  input  [31:0] Data_In,
  output Hit,
  output [31:0] Data_Out
);

  wire and_2_out, and_3_out, and_4_out, and_5_out, and_6_out, and_7_out, comparator_1_eq, decoder_1_out0,
       decoder_1_out1, decoder_1_out2, decoder_1_out3, decoder_2_out0, decoder_2_out1, decoder_2_out2,
       or_1_out, or_2_out, or_3_out, or_4_out, or_5_out, or_6_out, or_7_out, s_r_ff_1_q;
  wire [4:0] multiplexer_1_out;
  wire [7:0] conditional_increment_1_output, conditional_increment_2_output, conditional_increment_3_output,
       multiplexer_2_out, ram_1_data, ram_2_data, ram_3_data, ram_4_data;
  wire [15:0] multiplexer_3_out;
  wire [21:0] Tag_q;
  wire [31:0] bit_extender_1_out, bit_extender_2_out, multiplexer_4_out, shifter_1_out;

  or or_1 (or_1_out, Write, Set_Tag);
  Decoder #(.select(2), .disabled(0)) decoder_1 (
    .out0(decoder_1_out0), .out1(decoder_1_out1), .out2(decoder_1_out2), .out3(decoder_1_out3),
    .sel(Address[1:0]), .en(Sel));
  Decoder #(.select(2), .enable("false")) decoder_2 (
    .out0(decoder_2_out0), .out1(decoder_2_out1), .out2(decoder_2_out2), .sel(Mode[2:1]));  // open: out3
  S_R_Flip_Flop s_r_ff_1 (.S(Set_Tag), .clk(Clock), .Q(s_r_ff_1_q));  // open: R, Qn, preset, reset, en
  Register #(.width(22)) Tag (.D(Address[31:10]), .en(Set_Tag), .Q(Tag_q), .clk(Clock));  // open: clr
  or or_2 (or_2_out, decoder_1_out2, decoder_1_out3);
  Multiplexer #(.select(2), .width(5), .enable("false")) multiplexer_1 (
    .in0({5{1'b0}}), .in1(5'b01000), .in2(5'b10000), .in3(5'b11000), .out(multiplexer_1_out),
    .sel(Address[1:0]));
  and and_1 (Hit, s_r_ff_1_q, comparator_1_eq);
  Comparator #(.width(22)) comparator_1 (.a(Tag_q), .b(Address[31:10]), .eq(comparator_1_eq));  // open: gt, lt
  or or_3 (or_3_out, decoder_1_out1, decoder_1_out2, decoder_1_out3);
  Shifter #(.width(32)) shifter_1 (.in(Data_In), .\dist (multiplexer_1_out), .out(shifter_1_out));
  or or_4 (or_4_out, decoder_1_out0, decoder_2_out2, and_2_out);
  and and_2 (and_2_out, decoder_2_out1, decoder_1_out3);
  or or_5 (or_5_out, decoder_1_out1, decoder_2_out2, and_3_out);
  and and_3 (and_3_out, decoder_2_out1, decoder_1_out0);
  or or_6 (or_6_out, decoder_1_out2, decoder_2_out2, and_4_out);
  and and_4 (and_4_out, decoder_2_out1, decoder_1_out1);
  or or_7 (or_7_out, decoder_1_out3, decoder_2_out2, and_5_out);
  and and_5 (and_5_out, decoder_2_out1, decoder_1_out2);
  conditional_increment conditional_increment_1 (
    .\input (Address[9:2]), .\output (conditional_increment_1_output), .inc(or_3_out));
  conditional_increment conditional_increment_2 (
    .\input (Address[9:2]), .\output (conditional_increment_2_output), .inc(or_2_out));
  conditional_increment conditional_increment_3 (
    .\input (Address[9:2]), .\output (conditional_increment_3_output), .inc(decoder_1_out3));
  RAM #(.bus("separate")) ram_1 (
    .addr(conditional_increment_1_output), .din(shifter_1_out[7:0]), .data(ram_1_data), .str(or_1_out),
    .sel(or_4_out), .clk(Clock));  // open: ld, clr
  RAM #(.bus("separate")) ram_2 (
    .addr(conditional_increment_2_output), .din(shifter_1_out[15:8]), .data(ram_2_data), .str(or_1_out),
    .sel(or_5_out), .clk(Clock));  // open: ld, clr
  RAM #(.bus("separate")) ram_3 (
    .addr(conditional_increment_3_output), .din(shifter_1_out[23:16]), .data(ram_3_data), .str(or_1_out),
    .sel(or_6_out), .clk(Clock));  // open: ld, clr
  RAM #(.bus("separate")) ram_4 (
    .addr(Address[9:2]), .din(shifter_1_out[31:24]), .data(ram_4_data), .str(or_1_out), .sel(or_7_out),
    .clk(Clock));  // open: ld, clr
  Multiplexer #(.select(2), .width(8), .enable("false")) multiplexer_2 (
    .in0(ram_1_data), .in1(ram_2_data), .in2(ram_3_data), .in3(ram_4_data), .out(multiplexer_2_out),
    .sel(Address[1:0]));
  Multiplexer #(.select(2), .width(16), .enable("false")) multiplexer_3 (
    .in0({ram_2_data, ram_1_data}), .in1({ram_3_data, ram_2_data}), .in2({ram_4_data, ram_3_data}),
    .in3({ram_1_data, ram_4_data}), .out(multiplexer_3_out), .sel(Address[1:0]));
  Multiplexer #(.select(2), .width(32), .enable("false")) multiplexer_4 (
    .in0({ram_4_data, ram_3_data, ram_2_data, ram_1_data}),
    .in1({ram_3_data, ram_2_data, ram_1_data, ram_4_data}),
    .in2({ram_2_data, ram_1_data, ram_4_data, ram_3_data}),
    .in3({ram_1_data, ram_4_data, ram_3_data, ram_2_data}), .out(multiplexer_4_out), .sel(Address[1:0]));
  and and_6 (and_6_out, Mode[0], multiplexer_2_out[7]);
  assign bit_extender_1_out = {{24{and_6_out}}, multiplexer_2_out};  // Bit_Extender bit_extender_1
  and and_7 (and_7_out, Mode[0], multiplexer_3_out[15]);
  assign bit_extender_2_out = {{16{and_7_out}}, multiplexer_3_out};  // Bit_Extender bit_extender_2
  Multiplexer #(.select(2), .width(32), .enable("false")) multiplexer_5 (
    .in0(bit_extender_1_out), .in1(bit_extender_2_out), .in2(multiplexer_4_out), .out(Data_Out),
    .sel(Mode[2:1]));  // open: in3

  // Notes on the sheet:
  //   signed
  //   byte
  //   half
  //   word
  //   1KiB Cache Line
endmodule

module L1_Cache (
  input  [15:0] Load_Data,
  input  [31:0] Load_Address,
  input  [31:0] Address,
  input  [31:0] Data_in,
  input  [2:0] Mode,
  input  Clock,
  input  Write,
  input  Enable,
  output Cache_miss,
  output [31:0] Data_Out
);

  wire cache_line_1_hit, cache_line_2_hit, cache_line_3_hit, cache_line_4_hit, cache_line_5_hit,
       cache_line_6_hit, cache_line_7_hit, cache_line_8_hit, decoder_1_out0, decoder_1_out1, decoder_1_out2,
       decoder_1_out3, decoder_1_out4, decoder_1_out5, decoder_1_out6, decoder_1_out7, not_1_out;
  wire [2:0] lru_1_oldest_address, multiplexer_3_out, priority_encoder_1_out;
  wire [31:0] bit_extender_1_out, cache_line_1_data_out, cache_line_2_data_out, cache_line_3_data_out,
       cache_line_4_data_out, cache_line_5_data_out, cache_line_6_data_out, cache_line_7_data_out,
       cache_line_8_data_out, multiplexer_1_out, multiplexer_2_out;

  Multiplexer #(.width(32), .enable("false")) multiplexer_1 (
    .in0(Address), .in1(Load_Address), .out(multiplexer_1_out), .sel(Cache_miss));
  Multiplexer #(.width(32), .enable("false")) multiplexer_2 (
    .in0(Data_in), .in1(bit_extender_1_out), .out(multiplexer_2_out), .sel(Cache_miss));
  Multiplexer #(.width(3), .enable("false")) multiplexer_3 (
    .in0(Mode), .in1(3'b010), .out(multiplexer_3_out), .sel(Cache_miss));
  assign bit_extender_1_out = {{16{1'b0}}, Load_Data};  // Bit_Extender bit_extender_1
  Decoder #(.select(3), .disabled(0)) decoder_1 (
    .out0(decoder_1_out0), .out1(decoder_1_out1), .out2(decoder_1_out2), .out3(decoder_1_out3),
    .out4(decoder_1_out4), .out5(decoder_1_out5), .out6(decoder_1_out6), .out7(decoder_1_out7),
    .sel(lru_1_oldest_address), .en(Cache_miss));
  Cache_Line cache_line_1 (
    .Write(Write), .Set_Tag(decoder_1_out0), .Clock(Clock), .Address(multiplexer_1_out),
    .Mode(multiplexer_3_out), .Data_In(multiplexer_2_out), .Hit(cache_line_1_hit),
    .Data_Out(cache_line_1_data_out), .Sel(Enable));
  Cache_Line cache_line_2 (
    .Write(Write), .Set_Tag(decoder_1_out1), .Clock(Clock), .Address(multiplexer_1_out),
    .Mode(multiplexer_3_out), .Data_In(multiplexer_2_out), .Hit(cache_line_2_hit),
    .Data_Out(cache_line_2_data_out), .Sel(Enable));
  Cache_Line cache_line_3 (
    .Write(Write), .Set_Tag(decoder_1_out2), .Clock(Clock), .Address(multiplexer_1_out),
    .Mode(multiplexer_3_out), .Data_In(multiplexer_2_out), .Hit(cache_line_3_hit),
    .Data_Out(cache_line_3_data_out), .Sel(Enable));
  Cache_Line cache_line_4 (
    .Write(Write), .Set_Tag(decoder_1_out3), .Clock(Clock), .Address(multiplexer_1_out),
    .Mode(multiplexer_3_out), .Data_In(multiplexer_2_out), .Hit(cache_line_4_hit),
    .Data_Out(cache_line_4_data_out), .Sel(Enable));
  Cache_Line cache_line_5 (
    .Write(Write), .Set_Tag(decoder_1_out4), .Clock(Clock), .Address(multiplexer_1_out),
    .Mode(multiplexer_3_out), .Data_In(multiplexer_2_out), .Hit(cache_line_5_hit),
    .Data_Out(cache_line_5_data_out), .Sel(Enable));
  Cache_Line cache_line_6 (
    .Write(Write), .Set_Tag(decoder_1_out5), .Clock(Clock), .Address(multiplexer_1_out),
    .Mode(multiplexer_3_out), .Data_In(multiplexer_2_out), .Hit(cache_line_6_hit),
    .Data_Out(cache_line_6_data_out), .Sel(Enable));
  Cache_Line cache_line_7 (
    .Write(Write), .Set_Tag(decoder_1_out6), .Clock(Clock), .Address(multiplexer_1_out),
    .Mode(multiplexer_3_out), .Data_In(multiplexer_2_out), .Hit(cache_line_7_hit),
    .Data_Out(cache_line_7_data_out), .Sel(Enable));
  Cache_Line cache_line_8 (
    .Write(Write), .Set_Tag(decoder_1_out7), .Clock(Clock), .Address(multiplexer_1_out),
    .Mode(multiplexer_3_out), .Data_In(multiplexer_2_out), .Hit(cache_line_8_hit),
    .Data_Out(cache_line_8_data_out), .Sel(Enable));
  Multiplexer #(.select(3), .width(32)) multiplexer_4 (
    .in0(cache_line_1_data_out), .in1(cache_line_2_data_out), .in2(cache_line_3_data_out),
    .in3(cache_line_4_data_out), .in4(cache_line_5_data_out), .in5(cache_line_6_data_out),
    .in6(cache_line_7_data_out), .in7(cache_line_8_data_out), .out(Data_Out), .sel(priority_encoder_1_out),
    .en(not_1_out));
  not not_1 (not_1_out, Cache_miss);
  Priority_Encoder priority_encoder_1 (
    .in0(cache_line_1_hit), .in1(cache_line_2_hit), .in2(cache_line_3_hit), .in3(cache_line_4_hit),
    .in4(cache_line_5_hit), .in5(cache_line_6_hit), .in6(cache_line_7_hit), .in7(cache_line_8_hit),
    .out(priority_encoder_1_out), .en_out(Cache_miss));  // open: en_in, gs
  LRU lru_1 (.Cache_Address(priority_encoder_1_out), .Clock(Clock), .Oldest_Address(lru_1_oldest_address));
endmodule

module conditional_increment (
  input  inc,
  input  [7:0] \input ,
  output [7:0] \output 
);

  Adder adder_1 (.a(\input ), .b({8{1'b0}}), .out(\output ), .cin(inc));  // open: cout
endmodule

module LRU (
  input  [2:0] Cache_Address,
  input  Clock,
  output [2:0] Oldest_Address
);

  wire and_1_out, and_2_out, and_3_out, and_4_out, and_5_out, and_6_out, comparator_1_eq, comparator_2_eq,
       comparator_3_eq, comparator_4_eq, comparator_5_eq, comparator_6_eq, comparator_7_eq, not_1_out,
       not_2_out, not_3_out, not_4_out, not_5_out, not_6_out, not_7_out;
  wire [2:0] register_1_q, register_2_q, register_3_q, register_4_q, register_5_q, register_6_q, register_7_q;

  Comparator #(.width(3)) comparator_1 (.a(Cache_Address), .b(register_1_q), .eq(comparator_1_eq));  // open: gt, lt
  Register #(.width(3)) register_1 (.D(Cache_Address), .en(not_1_out), .Q(register_1_q), .clk(Clock));  // open: clr
  not not_1 (not_1_out, comparator_1_eq);
  Register #(.width(3)) register_2 (.D(register_1_q), .en(not_1_out), .Q(register_2_q), .clk(Clock));  // open: clr
  not not_2 (not_2_out, comparator_2_eq);
  Comparator #(.width(3)) comparator_2 (.a(Cache_Address), .b(register_2_q), .eq(comparator_2_eq));  // open: gt, lt
  Comparator #(.width(3)) comparator_3 (.a(Cache_Address), .b(register_3_q), .eq(comparator_3_eq));  // open: gt, lt
  and and_1 (and_1_out, not_2_out, not_1_out);
  Register #(.width(3)) register_3 (.D(register_2_q), .en(and_1_out), .Q(register_3_q), .clk(Clock));  // open: clr
  not not_3 (not_3_out, comparator_3_eq);
  and and_2 (and_2_out, not_3_out, and_1_out);
  not not_4 (not_4_out, comparator_4_eq);
  Comparator #(.width(3)) comparator_4 (.a(Cache_Address), .b(register_4_q), .eq(comparator_4_eq));  // open: gt, lt
  Register #(.width(3)) register_4 (.D(register_3_q), .en(and_2_out), .Q(register_4_q), .clk(Clock));  // open: clr
  and and_3 (and_3_out, not_4_out, and_2_out);
  Register #(.width(3)) register_5 (.D(register_4_q), .en(and_3_out), .Q(register_5_q), .clk(Clock));  // open: clr
  Comparator #(.width(3)) comparator_5 (.a(Cache_Address), .b(register_5_q), .eq(comparator_5_eq));  // open: gt, lt
  not not_5 (not_5_out, comparator_5_eq);
  and and_4 (and_4_out, not_5_out, and_3_out);
  not not_6 (not_6_out, comparator_6_eq);
  Comparator #(.width(3)) comparator_6 (.a(Cache_Address), .b(register_6_q), .eq(comparator_6_eq));  // open: gt, lt
  Register #(.width(3)) register_6 (.D(register_5_q), .en(and_4_out), .Q(register_6_q), .clk(Clock));  // open: clr
  and and_5 (and_5_out, not_6_out, and_4_out);
  not not_7 (not_7_out, comparator_7_eq);
  Comparator #(.width(3)) comparator_7 (.a(Cache_Address), .b(register_7_q), .eq(comparator_7_eq));  // open: gt, lt
  Register #(.width(3)) register_7 (.D(register_6_q), .en(and_5_out), .Q(register_7_q), .clk(Clock));  // open: clr
  and and_6 (and_6_out, not_7_out, and_5_out);
  Register #(.width(3)) register_8 (.D(register_7_q), .en(and_6_out), .Q(Oldest_Address), .clk(Clock));  // open: clr
endmodule

module FIFO_256x32 (
  input  [31:0] Requested_Address,
  input  Enqueue,
  input  Dequeue,
  input  Clock,
  output Full,
  output Empty,
  output [31:0] Queue_Out
);

  wire and_1_out, and_2_out, comparator_1_eq, or_1_out, Read_Address_carry, t_ff_1_q, t_ff_2_q,
       Write_Address_carry, xor_1_out;
  wire [7:0] multiplexer_1_out, Read_Address_q, Write_Address_q;

  and and_1 (and_1_out, Enqueue, Empty, ~Full);  // AND_Gate
  and and_2 (and_2_out, Dequeue, ~Empty, Full);  // AND_Gate
  Counter Read_Address (
    .count(and_2_out), .Q(Read_Address_q), .carry(Read_Address_carry), .clk(Clock));  // open: load, D, clr
  Counter Write_Address (
    .count(and_1_out), .Q(Write_Address_q), .carry(Write_Address_carry), .clk(Clock));  // open: load, D, clr
  Multiplexer #(.width(8), .disabled(0), .enable("false")) multiplexer_1 (
    .in0(Read_Address_q), .in1(Write_Address_q), .out(multiplexer_1_out), .sel(and_1_out));
  T_Flip_Flop t_ff_1 (.clk(Clock), .T(Read_Address_carry), .Q(t_ff_1_q));  // open: Qn, preset, reset, en
  xor xor_1 (xor_1_out, t_ff_1_q, t_ff_2_q);
  T_Flip_Flop t_ff_2 (.clk(Clock), .T(Write_Address_carry), .Q(t_ff_2_q));  // open: Qn, preset, reset, en
  or or_1 (or_1_out, and_1_out, and_2_out);
  and and_3 (Full, xor_1_out, comparator_1_eq);
  and and_4 (Empty, ~xor_1_out, comparator_1_eq);  // AND_Gate
  Comparator comparator_1 (.a(Read_Address_q), .b(Write_Address_q), .eq(comparator_1_eq));  // open: gt, lt
  RAM #(.dataWidth(32), .bus("separate")) ram_1 (
    .addr(multiplexer_1_out), .din(Requested_Address), .data(Queue_Out), .str(and_1_out), .sel(or_1_out),
    .clk(Clock), .ld(and_2_out));  // open: clr
endmodule

module _32bit_increment (
  input  [31:0] In,
  output [31:0] Out
);

  Adder #(.width(32)) adder_1 (.a(In), .b({32{1'b0}}), .out(Out), .cin(1'b1));  // open: cout
endmodule

module sdram_controller (
  input  [15:0] Data_from_RAM,
  input  clock,
  input  load,
  input  store,
  input  [15:0] data_in,
  output RAM_clk,
  output RAM_cke,
  output [15:0] Data_to_RAM,
  output [11:0] RAM_Address,
  output [1:0] Bank_Activate,
  output [1:0] Data_Mask,
  output RAM__cs,
  output nRAS,
  output nCAS,
  output nWE,
  output [15:0] data_out,
  output [23:0] addr,
  output data_valid
);

  wire decoder_1_out1, decoder_1_out2, decoder_1_out3, decoder_1_out4, decoder_1_out5, decoder_1_out6,
       decoder_1_out7, decoder_2_out1, decoder_2_out4, decoder_2_out6, decoder_2_out13, decoder_2_out18,
       nand_1_out, nor_1_out, or_2_out, or_4_out, priority_encoder_1_gs, priority_encoder_2_en_out;
  wire [1:1] decoder_1_out0;
  wire [2:0] priority_encoder_1_out, register_1_q, rom_1_data;
  wire [3:0] priority_encoder_2_out;
  wire [3:3] multiplexer_1_out;
  wire [4:0] Init_sequence_q;

  Priority_Encoder priority_encoder_1 (
    .in0(decoder_2_out18), .out(priority_encoder_1_out), .gs(priority_encoder_1_gs));  // open: in1, in2, in3, in4, in5, in6, in7, en_in, en_out
  ROM #(.addrWidth(3), .dataWidth(3)) rom_1 (
    .addr(priority_encoder_1_out), .data(rom_1_data), .sel(priority_encoder_1_gs));
  Register #(.width(3)) register_1 (
    .D(rom_1_data), .en(priority_encoder_1_gs), .Q(register_1_q), .clk(clock), .clr(or_2_out));
  buf or_1 (RAM_cke, decoder_1_out0[1]);  // OR_Gate
  Decoder #(.select(3), .disabled(0), .enable("false")) decoder_1 (
    .out0(decoder_1_out0[1]), .out1(decoder_1_out1), .out2(decoder_1_out2), .out3(decoder_1_out3),
    .out4(decoder_1_out4), .out5(decoder_1_out5), .out6(decoder_1_out6), .out7(decoder_1_out7),
    .sel(register_1_q));
  or or_2 (or_2_out, decoder_1_out7, decoder_1_out6, decoder_1_out5);
  Counter #(.width(5), .max('h1f)) Init_sequence (
    .count(decoder_1_out0[1]), .Q(Init_sequence_q), .clk(clock), .clr(or_2_out));  // open: load, D, carry
  Decoder #(.select(5), .disabled(0), .enable("false")) decoder_2 (
    .out1(decoder_2_out1), .out4(decoder_2_out4), .out6(decoder_2_out6), .out13(decoder_2_out13),
    .out18(decoder_2_out18), .sel(Init_sequence_q));  // open: out0, out2, out3, out5, out7, out8, out9, out10, out11, out12, out14, out15, out16, out17, out19, out20, out21, out22, out23, out24, out25, out26, out27, out28, out29, out30, out31
  assign Data_Mask = {2{decoder_1_out0[1]}};  // OR_Gate or_3, 2 bits wide OR_Gate
  nor nor_1 (nor_1_out, decoder_2_out1, decoder_2_out4, decoder_2_out6, decoder_2_out13);
  or or_4 (or_4_out, decoder_2_out6, decoder_2_out13);
  nand nand_1 (nand_1_out, decoder_1_out0[1], ~nor_1_out);  // NAND_Gate
  or or_5 (RAM__cs, multiplexer_1_out[3], nand_1_out);
  Priority_Encoder #(.select(4)) priority_encoder_2 (
    .in0(decoder_2_out4), .in1(or_4_out), .in2(decoder_2_out1), .out(priority_encoder_2_out),
    .en_out(priority_encoder_2_en_out));  // open: in3, in4, in5, in6, in7, in8, in9, in10, in11, in12, in13, in14, in15, gs, en_in
  Multiplexer #(.width(4), .enable("false")) multiplexer_1 (
    .in0(priority_encoder_2_out), .in1(4'b0111), .out({multiplexer_1_out[3], nRAS, nCAS, nWE}),
    .sel(priority_encoder_2_en_out));

  assign RAM_clk = clock;

  // Notes on the sheet:
  //   init
  //   idle
  //   write
  //   read
  //   refresh
  //   cke, ldqm, udqm
  //   prechargeall
  //   moderegset
  //   autorefresh
  //   autorefresh
  //   cs#
endmodule

module FIFO_512x16 (
  input  [15:0] Data_In,
  input  Enqueue,
  input  Dequeue,
  input  Clock,
  output Full,
  output Empty,
  output [15:0] Data_Out
);

  wire and_1_out, and_2_out, comparator_1_eq, or_1_out, Read_Address_carry, t_ff_1_q, t_ff_2_q,
       Write_Address_carry, xor_1_out;
  wire [8:0] multiplexer_1_out, Read_Address_q, Write_Address_q;

  and and_1 (and_1_out, Enqueue, ~Full);  // AND_Gate
  and and_2 (and_2_out, Dequeue, ~Empty);  // AND_Gate
  Counter #(.width(9), .max('h1ff)) Read_Address (
    .count(and_2_out), .Q(Read_Address_q), .carry(Read_Address_carry), .clk(Clock));  // open: load, D, clr
  Counter #(.width(9), .max('h1ff)) Write_Address (
    .count(and_1_out), .Q(Write_Address_q), .carry(Write_Address_carry), .clk(Clock));  // open: load, D, clr
  Multiplexer #(.width(9), .disabled(0), .enable("false")) multiplexer_1 (
    .in0(Read_Address_q), .in1(Write_Address_q), .out(multiplexer_1_out), .sel(and_1_out));
  T_Flip_Flop t_ff_1 (.clk(Clock), .T(Read_Address_carry), .Q(t_ff_1_q));  // open: Qn, preset, reset, en
  xor xor_1 (xor_1_out, t_ff_1_q, t_ff_2_q);
  T_Flip_Flop t_ff_2 (.clk(Clock), .T(Write_Address_carry), .Q(t_ff_2_q));  // open: Qn, preset, reset, en
  or or_1 (or_1_out, and_1_out, and_2_out);
  and and_3 (Full, xor_1_out, comparator_1_eq);
  and and_4 (Empty, ~xor_1_out, comparator_1_eq);  // AND_Gate
  Comparator #(.width(9)) comparator_1 (.a(Read_Address_q), .b(Write_Address_q), .eq(comparator_1_eq));  // open: gt, lt
  RAM #(.addrWidth(9), .dataWidth(16), .bus("separate")) ram_1 (
    .addr(multiplexer_1_out), .din(Data_In), .data(Data_Out), .str(and_1_out), .sel(or_1_out), .clk(Clock),
    .ld(and_2_out));  // open: clr
endmodule
