// Logisim project cache_rev2.circ as structural Verilog: 4 circuits, main circuit main
module main (
  input  [24:0] Address
);

  LRU16 lru16_1 ();  // open: slot, access, clock, oldest_slot
  bram bram_1 ();  // open: address, data_in, store, enable, clock, data_out
endmodule

module bram (
  input  [13:0] address,
  input  [7:0] data_in,
  input  store,
  input  enable,
  input  clock,
  output [7:0] data_out
);

  wire decoder_1_out0, decoder_1_out1, decoder_1_out2, decoder_1_out3, decoder_1_out4, decoder_1_out5,
       decoder_1_out6, decoder_1_out7, not_1_out, not_2_out, not_3_out, not_4_out, not_5_out, not_6_out,
       not_7_out, not_8_out;
  wire [7:0] ram_1_data, ram_2_data, ram_3_data, ram_4_data, ram_5_data, ram_6_data, ram_7_data, ram_8_data;

  Decoder #(.select(3), .disabled(0)) decoder_1 (
    .out0(decoder_1_out0), .out1(decoder_1_out1), .out2(decoder_1_out2), .out3(decoder_1_out3),
    .out4(decoder_1_out4), .out5(decoder_1_out5), .out6(decoder_1_out6), .out7(decoder_1_out7),
    .sel(address[13:11]), .en(enable));
  not not_1 (not_1_out, store);
  not not_2 (not_2_out, store);
  not not_3 (not_3_out, store);
  not not_4 (not_4_out, store);
  not not_5 (not_5_out, store);
  not not_6 (not_6_out, store);
  not not_7 (not_7_out, store);
  not not_8 (not_8_out, store);
  RAM #(.addrWidth(11), .bus("separate")) ram_1 (
    .addr(address[10:0]), .din(data_in), .data(ram_1_data), .str(store), .sel(decoder_1_out0), .clk(clock),
    .ld(not_1_out));  // open: clr
  RAM #(.addrWidth(11), .bus("separate")) ram_2 (
    .addr(address[10:0]), .din(data_in), .data(ram_2_data), .str(store), .sel(decoder_1_out1), .clk(clock),
    .ld(not_2_out));  // open: clr
  RAM #(.addrWidth(11), .bus("separate")) ram_3 (
    .addr(address[10:0]), .din(data_in), .data(ram_3_data), .str(store), .sel(decoder_1_out2), .clk(clock),
    .ld(not_3_out));  // open: clr
  RAM #(.addrWidth(11), .bus("separate")) ram_4 (
    .addr(address[10:0]), .din(data_in), .data(ram_4_data), .str(store), .sel(decoder_1_out3), .clk(clock),
    .ld(not_4_out));  // open: clr
  RAM #(.addrWidth(11), .bus("separate")) ram_5 (
    .addr(address[10:0]), .din(data_in), .data(ram_5_data), .str(store), .sel(decoder_1_out4), .clk(clock),
    .ld(not_5_out));  // open: clr
  RAM #(.addrWidth(11), .bus("separate")) ram_6 (
    .addr(address[10:0]), .din(data_in), .data(ram_6_data), .str(store), .sel(decoder_1_out5), .clk(clock),
    .ld(not_6_out));  // open: clr
  RAM #(.addrWidth(11), .bus("separate")) ram_7 (
    .addr(address[10:0]), .din(data_in), .data(ram_7_data), .str(store), .sel(decoder_1_out6), .clk(clock),
    .ld(not_7_out));  // open: clr
  RAM #(.addrWidth(11), .bus("separate")) ram_8 (
    .addr(address[10:0]), .din(data_in), .data(ram_8_data), .str(store), .sel(decoder_1_out7), .clk(clock),
    .ld(not_8_out));  // open: clr
  Multiplexer #(.select(3), .width(8), .enable("false")) multiplexer_1 (
    .in0(ram_1_data), .in1(ram_2_data), .in2(ram_3_data), .in3(ram_4_data), .in4(ram_5_data),
    .in5(ram_6_data), .in6(ram_7_data), .in7(ram_8_data), .out(data_out), .sel(address[13:11]));
endmodule

module LRU16 (
  input  [3:0] slot,
  input  access,
  input  clock,
  output [3:0] oldest_slot
);

  wire and_1_out, and_2_out, and_3_out, and_4_out, and_5_out, and_6_out, and_7_out, and_8_out, and_9_out,
       and_10_out, and_11_out, and_12_out, and_13_out, and_14_out, and_15_out, comparator_1_eq,
       comparator_2_eq, comparator_3_eq, comparator_4_eq, comparator_5_eq, comparator_6_eq, comparator_7_eq,
       comparator_8_eq, comparator_9_eq, comparator_10_eq, comparator_11_eq, comparator_12_eq,
       comparator_13_eq, comparator_14_eq, comparator_15_eq, not_1_out, not_2_out, not_3_out, not_4_out,
       not_5_out, not_6_out, not_7_out, not_8_out, not_9_out, not_10_out, not_11_out, not_12_out, not_13_out,
       not_14_out, not_15_out;
  wire [3:0] register_1_q, register_2_q, register_3_q, register_4_q, register_5_q, register_6_q,
       register_7_q, register_8_q, register_9_q, register_10_q, register_11_q, register_12_q, register_13_q,
       register_14_q, register_15_q;

  Comparator #(.width(4)) comparator_1 (.a(slot), .b(register_1_q), .eq(comparator_1_eq));  // open: gt, lt
  Register #(.width(4)) register_1 (.D(slot), .en(and_1_out), .Q(register_1_q), .clk(clock));  // open: clr
  not not_1 (not_1_out, comparator_1_eq);
  and and_1 (and_1_out, access, not_1_out);
  Register #(.width(4)) register_2 (.D(register_1_q), .en(and_1_out), .Q(register_2_q), .clk(clock));  // open: clr
  not not_2 (not_2_out, comparator_2_eq);
  Comparator #(.width(4)) comparator_2 (.a(slot), .b(register_2_q), .eq(comparator_2_eq));  // open: gt, lt
  Comparator #(.width(4)) comparator_3 (.a(slot), .b(register_3_q), .eq(comparator_3_eq));  // open: gt, lt
  and and_2 (and_2_out, not_2_out, and_1_out);
  Register #(.width(4)) register_3 (.D(register_2_q), .en(and_2_out), .Q(register_3_q), .clk(clock));  // open: clr
  not not_3 (not_3_out, comparator_3_eq);
  and and_3 (and_3_out, not_3_out, and_2_out);
  not not_4 (not_4_out, comparator_4_eq);
  Comparator #(.width(4)) comparator_4 (.a(slot), .b(register_4_q), .eq(comparator_4_eq));  // open: gt, lt
  Register #(.width(4)) register_4 (.D(register_3_q), .en(and_3_out), .Q(register_4_q), .clk(clock));  // open: clr
  and and_4 (and_4_out, not_4_out, and_3_out);
  Register #(.width(4)) register_5 (.D(register_4_q), .en(and_4_out), .Q(register_5_q), .clk(clock));  // open: clr
  not not_5 (not_5_out, comparator_5_eq);
  Comparator #(.width(4)) comparator_5 (.a(slot), .b(register_5_q), .eq(comparator_5_eq));  // open: gt, lt
  and and_5 (and_5_out, not_5_out, and_4_out);
  not not_6 (not_6_out, comparator_6_eq);
  Comparator #(.width(4)) comparator_6 (.a(slot), .b(register_6_q), .eq(comparator_6_eq));  // open: gt, lt
  Register #(.width(4)) register_6 (.D(register_5_q), .en(and_5_out), .Q(register_6_q), .clk(clock));  // open: clr
  and and_6 (and_6_out, not_6_out, and_5_out);
  Comparator #(.width(4)) comparator_7 (.a(slot), .b(register_7_q), .eq(comparator_7_eq));  // open: gt, lt
  not not_7 (not_7_out, comparator_7_eq);
  Register #(.width(4)) register_7 (.D(register_6_q), .en(and_6_out), .Q(register_7_q), .clk(clock));  // open: clr
  Comparator #(.width(4)) comparator_8 (.a(slot), .b(register_8_q), .eq(comparator_8_eq));  // open: gt, lt
  and and_7 (and_7_out, not_7_out, and_6_out);
  Register #(.width(4)) register_8 (.D(register_7_q), .en(and_7_out), .Q(register_8_q), .clk(clock));  // open: clr
  not not_8 (not_8_out, comparator_8_eq);
  and and_8 (and_8_out, not_8_out, and_7_out);
  Comparator #(.width(4)) comparator_9 (.a(slot), .b(register_9_q), .eq(comparator_9_eq));  // open: gt, lt
  not not_9 (not_9_out, comparator_9_eq);
  Register #(.width(4)) register_9 (.D(register_8_q), .en(and_8_out), .Q(register_9_q), .clk(clock));  // open: clr
  and and_9 (and_9_out, not_9_out, and_8_out);
  Comparator #(.width(4)) comparator_10 (.a(slot), .b(register_10_q), .eq(comparator_10_eq));  // open: gt, lt
  not not_10 (not_10_out, comparator_10_eq);
  Register #(.width(4)) register_10 (.D(register_9_q), .en(and_9_out), .Q(register_10_q), .clk(clock));  // open: clr
  Comparator #(.width(4)) comparator_11 (.a(slot), .b(register_11_q), .eq(comparator_11_eq));  // open: gt, lt
  and and_10 (and_10_out, not_10_out, and_9_out);
  Register #(.width(4)) register_11 (.D(register_10_q), .en(and_10_out), .Q(register_11_q), .clk(clock));  // open: clr
  not not_11 (not_11_out, comparator_11_eq);
  and and_11 (and_11_out, not_11_out, and_10_out);
  not not_12 (not_12_out, comparator_12_eq);
  Comparator #(.width(4)) comparator_12 (.a(slot), .b(register_12_q), .eq(comparator_12_eq));  // open: gt, lt
  Register #(.width(4)) register_12 (.D(register_11_q), .en(and_11_out), .Q(register_12_q), .clk(clock));  // open: clr
  and and_12 (and_12_out, not_12_out, and_11_out);
  not not_13 (not_13_out, comparator_13_eq);
  Comparator #(.width(4)) comparator_13 (.a(slot), .b(register_13_q), .eq(comparator_13_eq));  // open: gt, lt
  Register #(.width(4)) register_13 (.D(register_12_q), .en(and_12_out), .Q(register_13_q), .clk(clock));  // open: clr
  Comparator #(.width(4)) comparator_14 (.a(slot), .b(register_14_q), .eq(comparator_14_eq));  // open: gt, lt
  and and_13 (and_13_out, not_13_out, and_12_out);
  Register #(.width(4)) register_14 (.D(register_13_q), .en(and_13_out), .Q(register_14_q), .clk(clock));  // open: clr
  not not_14 (not_14_out, comparator_14_eq);
  and and_14 (and_14_out, not_14_out, and_13_out);
  Comparator #(.width(4)) comparator_15 (.a(slot), .b(register_15_q), .eq(comparator_15_eq));  // open: gt, lt
  not not_15 (not_15_out, comparator_15_eq);
  Register #(.width(4)) register_15 (.D(register_14_q), .en(and_14_out), .Q(register_15_q), .clk(clock));  // open: clr
  and and_15 (and_15_out, not_15_out, and_14_out);
  Register #(.width(4)) register_16 (.D(register_15_q), .en(and_15_out), .Q(oldest_slot), .clk(clock));  // open: clr
endmodule

module tags (
  input  in_1,
  input  [3:0] LRU
);

  wire d_ff_1_qn, d_ff_2_qn, d_ff_3_qn, d_ff_4_qn, d_ff_5_qn, d_ff_6_qn, d_ff_7_qn, d_ff_8_qn, d_ff_9_qn,
       d_ff_10_qn, d_ff_11_qn, d_ff_12_qn, d_ff_13_qn, d_ff_14_qn, d_ff_15_qn, decoder_1_out0,
       decoder_1_out1, decoder_1_out2, decoder_1_out3, or_1_out, undriven_2, undriven_3, undriven_4,
       undriven_5, undriven_6, undriven_7, undriven_8, undriven_9, undriven_10, undriven_11, undriven_12,
       undriven_13;
  wire [3:0] multiplexer_1_out, priority_encoder_1_out, subtractor_1_out;
  wire [10:0] register_1_q, register_2_q, register_3_q, register_4_q, register_5_q, register_6_q,
       register_7_q, register_8_q, register_9_q, register_10_q, register_11_q, register_12_q, register_13_q,
       register_14_q, register_15_q, register_16_q, undriven;

  Multiplexer #(.width(4), .enable("false")) multiplexer_1 (
    .in0(LRU), .in1(subtractor_1_out), .out(multiplexer_1_out), .sel(or_1_out));
  Decoder #(.select(4)) decoder_1 (
    .out0(decoder_1_out0), .out1(decoder_1_out1), .out2(decoder_1_out2), .out3(decoder_1_out3),
    .sel(multiplexer_1_out));  // open: out4, out5, out6, out7, out8, out9, out10, out11, out12, out13, out14, out15, en
  D_Flip_Flop d_ff_1 (.clk(in_1), .D(decoder_1_out0), .Qn(d_ff_1_qn), .en(d_ff_1_qn));  // open: Q, preset, reset
  Register #(.width(11)) register_1 (.D(undriven), .en(decoder_1_out0), .Q(register_1_q), .clk(in_1));  // open: clr
  D_Flip_Flop d_ff_2 (.clk(in_1), .D(decoder_1_out1), .Qn(d_ff_2_qn), .en(d_ff_2_qn));  // open: Q, preset, reset
  Register #(.width(11)) register_2 (.D(undriven), .en(decoder_1_out1), .Q(register_2_q), .clk(in_1));  // open: clr
  D_Flip_Flop d_ff_3 (.clk(in_1), .D(decoder_1_out2), .Qn(d_ff_3_qn), .en(d_ff_3_qn));  // open: Q, preset, reset
  Register #(.width(11)) register_3 (.D(undriven), .en(decoder_1_out2), .Q(register_3_q), .clk(in_1));  // open: clr
  D_Flip_Flop d_ff_4 (.clk(in_1), .D(decoder_1_out3), .Qn(d_ff_4_qn), .en(d_ff_4_qn));  // open: Q, preset, reset
  Register #(.width(11)) register_4 (.D(undriven), .en(decoder_1_out3), .Q(register_4_q), .clk(in_1));  // open: clr
  D_Flip_Flop d_ff_5 (.clk(in_1), .D(undriven_2), .Qn(d_ff_5_qn), .en(d_ff_5_qn));  // open: Q, preset, reset
  Register #(.width(11)) register_5 (.D(undriven), .en(undriven_2), .Q(register_5_q), .clk(in_1));  // open: clr
  D_Flip_Flop d_ff_6 (.clk(in_1), .D(undriven_3), .Qn(d_ff_6_qn), .en(d_ff_6_qn));  // open: Q, preset, reset
  Register #(.width(11)) register_6 (.D(undriven), .en(undriven_3), .Q(register_6_q), .clk(in_1));  // open: clr
  D_Flip_Flop d_ff_7 (.clk(in_1), .D(undriven_4), .Qn(d_ff_7_qn), .en(d_ff_7_qn));  // open: Q, preset, reset
  Register #(.width(11)) register_7 (.D(undriven), .en(undriven_4), .Q(register_7_q), .clk(in_1));  // open: clr
  D_Flip_Flop d_ff_8 (.clk(in_1), .D(undriven_5), .Qn(d_ff_8_qn), .en(d_ff_8_qn));  // open: Q, preset, reset
  Register #(.width(11)) register_8 (.D(undriven), .en(undriven_5), .Q(register_8_q), .clk(in_1));  // open: clr
  D_Flip_Flop d_ff_9 (.clk(in_1), .D(undriven_6), .Qn(d_ff_9_qn), .en(d_ff_9_qn));  // open: Q, preset, reset
  Register #(.width(11)) register_9 (.D(undriven), .en(undriven_6), .Q(register_9_q), .clk(in_1));  // open: clr
  D_Flip_Flop d_ff_10 (.clk(in_1), .D(undriven_7), .Qn(d_ff_10_qn), .en(d_ff_10_qn));  // open: Q, preset, reset
  Register #(.width(11)) register_10 (.D(undriven), .en(undriven_7), .Q(register_10_q), .clk(in_1));  // open: clr
  D_Flip_Flop d_ff_11 (.clk(in_1), .D(undriven_8), .Qn(d_ff_11_qn), .en(d_ff_11_qn));  // open: Q, preset, reset
  Register #(.width(11)) register_11 (.D(undriven), .en(undriven_8), .Q(register_11_q), .clk(in_1));  // open: clr
  D_Flip_Flop d_ff_12 (.clk(in_1), .D(undriven_9), .Qn(d_ff_12_qn), .en(d_ff_12_qn));  // open: Q, preset, reset
  Register #(.width(11)) register_12 (.D(undriven), .en(undriven_9), .Q(register_12_q), .clk(in_1));  // open: clr
  D_Flip_Flop d_ff_13 (.clk(in_1), .D(undriven_10), .Qn(d_ff_13_qn), .en(d_ff_13_qn));  // open: Q, preset, reset
  Register #(.width(11)) register_13 (.D(undriven), .en(undriven_10), .Q(register_13_q), .clk(in_1));  // open: clr
  D_Flip_Flop d_ff_14 (.clk(in_1), .D(undriven_11), .Qn(d_ff_14_qn), .en(d_ff_14_qn));  // open: Q, preset, reset
  Register #(.width(11)) register_14 (.D(undriven), .en(undriven_11), .Q(register_14_q), .clk(in_1));  // open: clr
  D_Flip_Flop d_ff_15 (.clk(in_1), .D(undriven_12), .Qn(d_ff_15_qn), .en(d_ff_15_qn));  // open: Q, preset, reset
  Register #(.width(11)) register_15 (.D(undriven), .en(undriven_12), .Q(register_15_q), .clk(in_1));  // open: clr
  D_Flip_Flop d_ff_16 (.clk(in_1), .D(undriven_13), .Qn(d_ff_15_qn), .en(d_ff_15_qn));  // open: Q, preset, reset
  Register #(.width(11)) register_16 (.D(undriven), .en(undriven_13), .Q(register_16_q), .clk(in_1));  // open: clr
  or or_1 (or_1_out, d_ff_8_qn, d_ff_1_qn, d_ff_2_qn, d_ff_3_qn, d_ff_4_qn, d_ff_5_qn, d_ff_6_qn, d_ff_7_qn, d_ff_9_qn, d_ff_10_qn, d_ff_11_qn, d_ff_12_qn, d_ff_13_qn, d_ff_14_qn, d_ff_15_qn, d_ff_15_qn);
  Priority_Encoder #(.select(4)) priority_encoder_1 (
    .in0(d_ff_15_qn), .in1(d_ff_15_qn), .in2(d_ff_14_qn), .in3(d_ff_13_qn), .in4(d_ff_12_qn),
    .in5(d_ff_11_qn), .in6(d_ff_10_qn), .in7(d_ff_9_qn), .in8(d_ff_8_qn), .in9(d_ff_7_qn), .in10(d_ff_6_qn),
    .in11(d_ff_5_qn), .in12(d_ff_4_qn), .in13(d_ff_3_qn), .in14(d_ff_2_qn), .in15(d_ff_1_qn),
    .out(priority_encoder_1_out));  // open: gs, en_out, en_in
  Subtractor #(.width(4)) subtractor_1 (
    .a(4'b1111), .b(priority_encoder_1_out), .out(subtractor_1_out));  // open: bin, bout
endmodule
