// Logisim project fifo.circ as structural Verilog
module fifo_asynch (
  input  enqueue_clock,
  input  enqueue,
  input  dequeue,
  input  dequeue_clock
);

  wire and_1_out, and_2_out, and_3_out, and_4_out, and_5_out, and_6_out, comparator_1_eq, or_1_out, or_2_out,
       read_ptr_carry, t_ff_1_q, t_ff_2_q, write_ptr_carry, xor_1_out;
  wire [3:0] read_ptr_q, write_ptr_q;

  T_Flip_Flop t_ff_1 (
    .clk(enqueue_clock), .T(write_ptr_carry), .Q(t_ff_1_q), .en(and_3_out));  // open: Qn, preset, reset
  Counter #(.width(4), .max('hf)) write_ptr (
    .count(and_3_out), .Q(write_ptr_q), .carry(write_ptr_carry), .clk(enqueue_clock));  // open: load, D, clr
  T_Flip_Flop t_ff_2 (
    .clk(dequeue_clock), .T(read_ptr_carry), .Q(t_ff_2_q), .en(and_4_out));  // open: Qn, preset, reset
  Counter #(.width(4), .max('hf)) read_ptr (
    .count(and_4_out), .Q(read_ptr_q), .carry(read_ptr_carry), .clk(dequeue_clock));  // open: load, D, clr
  and and_1 (and_1_out, and_5_out, dequeue);
  and and_2 (and_2_out, enqueue, and_6_out);
  xor xor_1 (xor_1_out, t_ff_1_q, t_ff_2_q);
  and and_3 (and_3_out, enqueue, ~and_1_out);  // AND_Gate
  and and_4 (and_4_out, dequeue, ~and_2_out);  // AND_Gate
  Comparator #(.width(4)) comparator_1 (.a(write_ptr_q), .b(read_ptr_q), .eq(comparator_1_eq));  // open: gt, lt
  or or_1 (or_1_out, and_3_out, and_4_out);
  or or_2 (or_2_out, enqueue_clock, dequeue_clock);
  and and_5 (and_5_out, xor_1_out, comparator_1_eq);
  and and_6 (and_6_out, ~xor_1_out, comparator_1_eq);  // AND_Gate

  // Notes on the sheet:
  //   full
  //   empty
endmodule

module _4x4_dualport_ram (
  input  [1:0] addra,
  input  ena,
  input  [3:0] dina,
  input  wea,
  input  clka,
  input  web,
  input  clkb,
  input  [3:0] dinb,
  input  enb,
  input  [1:0] addrb,
  output [3:0] doa,
  output [3:0] dob
);

  wire decoder_1_out0, decoder_1_out1, decoder_1_out2, decoder_1_out3, decoder_2_out0, decoder_2_out1,
       decoder_2_out2, decoder_2_out3;
  wire [1:0] controlled_buffer_5_out, controlled_buffer_6_out, controlled_buffer_7_out,
       controlled_buffer_8_out;
  wire [3:0] controlled_buffer_1_out, controlled_buffer_2_out, controlled_buffer_3_out,
       controlled_buffer_4_out, register_1_q, register_2_q, register_3_q, register_4_q;

  Decoder #(.select(2), .disabled(0)) decoder_1 (
    .out0(decoder_1_out0), .out1(decoder_1_out1), .out2(decoder_1_out2), .out3(decoder_1_out3), .sel(addra),
    .en(ena));
  assign controlled_buffer_1_out = decoder_1_out0 ? dina : 4'bz;  // Controlled_Buffer controlled_buffer_1
  assign controlled_buffer_2_out = decoder_1_out1 ? dina : 4'bz;  // Controlled_Buffer controlled_buffer_2
  assign controlled_buffer_3_out = decoder_1_out2 ? dina : 4'bz;  // Controlled_Buffer controlled_buffer_3
  assign controlled_buffer_4_out = decoder_1_out3 ? dina : 4'bz;  // Controlled_Buffer controlled_buffer_4
  assign controlled_buffer_5_out = decoder_1_out0 ? {clka, wea} : 2'bz;  // Controlled_Buffer controlled_buffer_5
  assign controlled_buffer_6_out = decoder_1_out1 ? {clka, wea} : 2'bz;  // Controlled_Buffer controlled_buffer_6
  assign controlled_buffer_7_out = decoder_1_out2 ? {clka, wea} : 2'bz;  // Controlled_Buffer controlled_buffer_7
  assign controlled_buffer_8_out = decoder_1_out3 ? {clka, wea} : 2'bz;  // Controlled_Buffer controlled_buffer_8
  assign controlled_buffer_5_out = decoder_2_out0 ? {clkb, web} : 2'bz;  // Controlled_Buffer controlled_buffer_9
  assign controlled_buffer_6_out = decoder_2_out1 ? {clkb, web} : 2'bz;  // Controlled_Buffer controlled_buffer_10
  assign controlled_buffer_7_out = decoder_2_out2 ? {clkb, web} : 2'bz;  // Controlled_Buffer controlled_buffer_11
  assign controlled_buffer_8_out = decoder_2_out3 ? {clkb, web} : 2'bz;  // Controlled_Buffer controlled_buffer_12
  assign controlled_buffer_1_out = decoder_2_out0 ? dinb : 4'bz;  // Controlled_Buffer controlled_buffer_13
  assign controlled_buffer_2_out = decoder_2_out1 ? dinb : 4'bz;  // Controlled_Buffer controlled_buffer_14
  assign controlled_buffer_3_out = decoder_2_out2 ? dinb : 4'bz;  // Controlled_Buffer controlled_buffer_15
  assign controlled_buffer_4_out = decoder_2_out3 ? dinb : 4'bz;  // Controlled_Buffer controlled_buffer_16
  Decoder #(.select(2), .disabled(0)) decoder_2 (
    .out0(decoder_2_out0), .out1(decoder_2_out1), .out2(decoder_2_out2), .out3(decoder_2_out3), .sel(addrb),
    .en(enb));
  Register #(.width(4)) register_1 (
    .D(controlled_buffer_1_out), .en(controlled_buffer_5_out[0]), .Q(register_1_q),
    .clk(controlled_buffer_5_out[1]));  // open: clr
  Register #(.width(4)) register_2 (
    .D(controlled_buffer_2_out), .en(controlled_buffer_6_out[0]), .Q(register_2_q),
    .clk(controlled_buffer_6_out[1]));  // open: clr
  Register #(.width(4)) register_3 (
    .D(controlled_buffer_3_out), .en(controlled_buffer_7_out[0]), .Q(register_3_q),
    .clk(controlled_buffer_7_out[1]));  // open: clr
  Register #(.width(4)) register_4 (
    .D(controlled_buffer_4_out), .en(controlled_buffer_8_out[0]), .Q(register_4_q),
    .clk(controlled_buffer_8_out[1]));  // open: clr
  Multiplexer #(.select(2), .width(4)) multiplexer_1 (
    .in0(register_1_q), .in1(register_2_q), .in2(register_3_q), .in3(register_4_q), .out(doa), .sel(addra),
    .en(ena));
  Multiplexer #(.select(2), .width(4)) multiplexer_2 (
    .in0(register_1_q), .in1(register_2_q), .in2(register_3_q), .in3(register_4_q), .out(dob), .sel(addrb),
    .en(enb));
endmodule

module _16x4_dualport_ram (
  input  [3:0] addra,
  input  ena,
  input  [3:0] dina,
  input  wea,
  input  clka,
  input  [3:0] addrb,
  input  enb,
  input  [3:0] dinb,
  input  web,
  input  clkb,
  output [3:0] doa,
  output [3:0] dob
);

  wire demultiplexer_1_out0, demultiplexer_1_out1, demultiplexer_1_out2, demultiplexer_1_out3,
       demultiplexer_2_out0, demultiplexer_2_out1, demultiplexer_2_out2, demultiplexer_2_out3;
  wire [3:0] n4x4_dualport_ram_1_doa, n4x4_dualport_ram_1_dob, n4x4_dualport_ram_2_doa,
       n4x4_dualport_ram_2_dob, n4x4_dualport_ram_3_doa, n4x4_dualport_ram_3_dob, n4x4_dualport_ram_4_doa,
       n4x4_dualport_ram_4_dob;

  Demultiplexer #(.select(2), .enable("false")) demultiplexer_1 (
    .out0(demultiplexer_1_out0), .out1(demultiplexer_1_out1), .out2(demultiplexer_1_out2),
    .out3(demultiplexer_1_out3), .in(ena), .sel(addra[3:2]));
  Demultiplexer #(.select(2), .enable("false")) demultiplexer_2 (
    .out0(demultiplexer_2_out0), .out1(demultiplexer_2_out1), .out2(demultiplexer_2_out2),
    .out3(demultiplexer_2_out3), .in(enb), .sel(addrb[3:2]));
  _4x4_dualport_ram u_4x4_dualport_ram_1 (
    .addra(addra[1:0]), .ena(demultiplexer_1_out0), .dina(dina), .wea(wea), .clka(clka), .web(web),
    .clkb(clkb), .dinb(dinb), .enb(demultiplexer_2_out0), .addrb(addrb[1:0]), .doa(n4x4_dualport_ram_1_doa),
    .dob(n4x4_dualport_ram_1_dob));
  _4x4_dualport_ram u_4x4_dualport_ram_2 (
    .addra(addra[1:0]), .ena(demultiplexer_1_out1), .dina(dina), .wea(wea), .clka(clka), .web(web),
    .clkb(clkb), .dinb(dinb), .enb(demultiplexer_2_out1), .addrb(addrb[1:0]), .doa(n4x4_dualport_ram_2_doa),
    .dob(n4x4_dualport_ram_2_dob));
  _4x4_dualport_ram u_4x4_dualport_ram_3 (
    .addra(addra[1:0]), .ena(demultiplexer_1_out2), .dina(dina), .wea(wea), .clka(clka), .web(web),
    .clkb(clkb), .dinb(dinb), .enb(demultiplexer_2_out2), .addrb(addrb[1:0]), .doa(n4x4_dualport_ram_3_doa),
    .dob(n4x4_dualport_ram_3_dob));
  _4x4_dualport_ram u_4x4_dualport_ram_4 (
    .addra(addra[1:0]), .ena(demultiplexer_1_out3), .dina(dina), .wea(wea), .clka(clka), .web(web),
    .clkb(clkb), .dinb(dinb), .enb(demultiplexer_2_out3), .addrb(addrb[1:0]), .doa(n4x4_dualport_ram_4_doa),
    .dob(n4x4_dualport_ram_4_dob));
  Multiplexer #(.select(2), .width(4), .enable("false")) multiplexer_1 (
    .in0(n4x4_dualport_ram_1_doa), .in1(n4x4_dualport_ram_2_doa), .in2(n4x4_dualport_ram_3_doa),
    .in3(n4x4_dualport_ram_4_doa), .out(doa), .sel(addra[3:2]));
  Multiplexer #(.select(2), .width(4), .enable("false")) multiplexer_2 (
    .in0(n4x4_dualport_ram_1_dob), .in1(n4x4_dualport_ram_2_dob), .in2(n4x4_dualport_ram_3_dob),
    .in3(n4x4_dualport_ram_4_dob), .out(dob), .sel(addrb[3:2]));
endmodule
