// Logisim project shifter.circ as structural Verilog: 1 circuit, main circuit main
module main (
  input  [4:0] shamt,
  input  [31:0] data,
  output [31:0] \output 
);

  wire [31:0] multiplexer_1_out, multiplexer_2_out, multiplexer_3_out, multiplexer_4_out;

  Multiplexer #(.width(32), .disabled(0), .enable("false")) multiplexer_1 (
    .in0(data), .in1({data[15:0], {16{1'b0}}}), .out(multiplexer_1_out), .sel(shamt[4]));
  Multiplexer #(.width(32), .disabled(0), .enable("false")) multiplexer_2 (
    .in0(multiplexer_1_out), .in1({multiplexer_1_out[23:0], {8{1'b0}}}), .out(multiplexer_2_out),
    .sel(shamt[3]));
  Multiplexer #(.width(32), .disabled(0), .enable("false")) multiplexer_3 (
    .in0(multiplexer_2_out), .in1({multiplexer_2_out[27:0], 4'b0000}), .out(multiplexer_3_out), .sel(shamt[2]));
  Multiplexer #(.width(32), .disabled(0), .enable("false")) multiplexer_4 (
    .in0(multiplexer_3_out), .in1({multiplexer_3_out[29:0], 2'b00}), .out(multiplexer_4_out), .sel(shamt[1]));
  Multiplexer #(.width(32), .disabled(0), .enable("false")) multiplexer_5 (
    .in0(multiplexer_4_out), .in1({multiplexer_4_out[30:0], 1'b0}), .out(\output ), .sel(shamt[0]));
endmodule
